# Fritzing sketch Uno-esp8266 (saved by Fritzing 0.9.5d)
breadboards: 1

parts:
  Part1 = Arduino Uno (Rev3) - ICSP
  Espessif_Serial_Wifi_Modul_1 = ESP8266 ESP01 [part_number=ESP8266 package=THT]
  U1 = LCD-16X2 [package=lcd-16x2_noholes]  # not connected
  DHT1 = DHT11 Humitidy and Temperature Sensor
  R1 = Trimmer Potentiometer [maximum_resistance=10kΩ package=THT]

nets:
  GND: Part1.GND, Espessif_Serial_Wifi_Modul_1.GND, R1.leg2
  N1: Part1.D2, Espessif_Serial_Wifi_Modul_1.TXD
  N2: Part1.D3_PWM, Espessif_Serial_Wifi_Modul_1.RXD
  N3: Part1.D4, DHT1.DATA
  3V3: Part1.3V3, Espessif_Serial_Wifi_Modul_1.VCC
  N4: Part1.5V, R1.leg1

custom parts:
  ESP8266 ESP01: Generic WiFi Module based on the ESP8266 with onboard PCB antenna and UART communications
  DHT11 Humitidy and Temperature Sensor: DHT11 Humidity and Temperature Sensor
